// Logisim project mupc.circ as structural Verilog
module main (
  input  in_1,
  input  in_2
);

  wire and_1_out, and_2_out, CLOCK_EXEC, CLOCK_FETCH, comparator_1_eq, d_ff_1_q, decoder_1_out0,
       decoder_1_out1, decoder_1_out2, decoder_1_out3, IMM_FLAG_INV, multiplexer_3_out, not_2_out, not_3_out;
  wire [1:0] REG_SELECT;
  wire [7:0] adder_2_out, adder_3_out, adder_4_out, adder_5_out, adder_6_out, and_3_out, bit_extender_1_out,
       bit_extender_2_out, IMMEDIATE, INSTRUCTION, multiplexer_5_out, multiplexer_6_out, multiplexer_7_out,
       multiplexer_8_out, multiplexer_9_out, or_1_out, ram_1_dout, random_1_out, REG_1, REG_2, REG_A, REG_B,
       REG_IN, shifter_1_out, subtractor_1_out, subtractor_2_out, xor_1_out;
  wire [15:0] adder_1_out, REG_ADDRESS, register_1_q;

  Clock clock_1 (.out(CLOCK_FETCH));
  Adder #(.width(16)) adder_1 (.a(register_1_q), .b(16'h1), .out(adder_1_out));  // open: cin, cout
  not not_1 (CLOCK_EXEC, CLOCK_FETCH);
  Decoder #(.select(2)) decoder_1 (
    .out0(decoder_1_out0), .out1(decoder_1_out1), .out2(decoder_1_out2), .out3(decoder_1_out3),
    .sel(REG_SELECT), .en(IMM_FLAG_INV));
  Multiplexer #(.select(2), .width(8)) multiplexer_1 (
    .in0(REG_A), .in1(REG_B), .in2(REG_ADDRESS[7:0]), .in3(REG_ADDRESS[15:8]), .out(REG_1),
    .sel(INSTRUCTION[3:2]));
  Multiplexer #(.select(2), .width(8)) multiplexer_2 (
    .in0(REG_A), .in1(REG_B), .in2(REG_ADDRESS[7:0]), .in3(REG_ADDRESS[15:8]), .out(REG_2),
    .sel(INSTRUCTION[1:0]));
  Register #(.width(16)) register_1 (.D(adder_1_out), .en(CLOCK_EXEC), .clk(CLOCK_EXEC), .Q(register_1_q), .clr(in_1));
  Comparator #(.width(4)) comparator_1 (.a(4'b1111), .b(INSTRUCTION[7:4]), .eq(comparator_1_eq));  // open: gt, lt
  not not_2 (not_2_out, d_ff_1_q);
  RAM #(.addrWidth(16), .asyncread("true")) ram_1 (
    .addr(register_1_q), .oe(1'b1), .clk(CLOCK_EXEC), .dout(ram_1_dout));  // open: we, din
  Register register_2 (.D(REG_IN), .en(decoder_1_out0), .clk(CLOCK_EXEC), .Q(REG_A), .clr(in_1));
  Register register_3 (.D(REG_IN), .en(decoder_1_out1), .clk(CLOCK_EXEC), .Q(REG_B), .clr(in_1));
  Register register_4 (.D(REG_IN), .en(decoder_1_out2), .clk(CLOCK_EXEC), .Q(REG_ADDRESS[7:0]), .clr(in_1));
  Register register_5 (.D(REG_IN), .en(decoder_1_out3), .clk(CLOCK_EXEC), .Q(REG_ADDRESS[15:8]), .clr(in_1));
  Multiplexer #(.select(4)) multiplexer_3 (
    .in0(1'b0), .in1(1'b0), .in2(1'b0), .in3(1'b0), .in4(1'b0), .in5(1'b0), .in6(1'b0), .in7(1'b1),
    .in8(1'b1), .in9(1'b0), .in10(1'b0), .in11(1'b0), .in12(1'b1), .in13(1'b1), .in14(1'b1), .in15(1'b1),
    .out(multiplexer_3_out), .sel(INSTRUCTION[7:4]));
  D_Flip_Flop d_ff_1 (.D(and_1_out), .clk(CLOCK_FETCH), .Q(d_ff_1_q), .Qn(IMM_FLAG_INV), .reset(in_1));  // open: preset
  and and_1 (and_1_out, not_2_out, comparator_1_eq);
  Multiplexer #(.width(2)) multiplexer_4 (
    .in0(INSTRUCTION[3:2]), .in1(INSTRUCTION[1:0]), .out(REG_SELECT), .sel(multiplexer_3_out));
  and and_2 (and_2_out, IMM_FLAG_INV, CLOCK_EXEC);
  not not_3 (not_3_out, and_2_out);
  Register register_6 (.D(ram_1_dout), .en(and_2_out), .clk(and_2_out), .Q(INSTRUCTION), .clr(in_1));
  Register register_7 (.D(ram_1_dout), .en(not_3_out), .clk(not_3_out), .Q(IMMEDIATE), .clr(in_1));
  assign bit_extender_1_out = {{7{1'b0}}, in_2};  // Bit_Extender bit_extender_1
  assign bit_extender_2_out = {{7{1'b0}}, in_2};  // Bit_Extender bit_extender_2
  Random random_1 (.clk(CLOCK_FETCH), .out(random_1_out));  // open: clr, next
  Adder adder_2 (.a(REG_2), .b(8'h1), .out(adder_2_out));  // open: cin, cout
  Subtractor subtractor_1 (.a(REG_2), .b(8'h1), .out(subtractor_1_out));  // open: bin, bout
  Adder adder_3 (.a(REG_2), .b(bit_extender_1_out), .out(adder_3_out));  // open: cin, cout
  Adder adder_4 (.a(REG_2), .b(bit_extender_2_out), .out(adder_4_out));  // open: cin, cout
  Adder adder_5 (.a(IMMEDIATE), .b(REG_2), .out(adder_5_out));  // open: cin, cout
  Adder adder_6 (.a(REG_1), .b(REG_2), .out(adder_6_out));  // open: cin, cout
  Subtractor subtractor_2 (.a(REG_1), .b(REG_2), .out(subtractor_2_out));  // open: bin, bout
  assign and_3_out = REG_1 & REG_2;  // AND_Gate and_3, 8 bits wide
  assign or_1_out = REG_1 | REG_2;  // OR_Gate or_1, 8 bits wide
  assign xor_1_out = REG_1 ^ REG_2;  // XOR_Gate xor_1, 8 bits wide
  Shifter #(.shift("lr")) shifter_1 (.in(REG_1), .\dist (REG_2[2:0]), .out(shifter_1_out));
  Multiplexer #(.select(2), .width(8)) multiplexer_5 (
    .in0(adder_2_out), .in1(subtractor_1_out), .in2(adder_3_out), .in3(adder_4_out), .out(multiplexer_5_out),
    .sel(INSTRUCTION[3:2]));
  Multiplexer #(.select(2), .width(8)) multiplexer_6 (
    .in0(REG_2), .in1(REG_2), .in2(REG_2), .in3(REG_2), .out(multiplexer_6_out), .sel(INSTRUCTION[3:2]));
  Multiplexer #(.select(2), .width(8)) multiplexer_7 (
    .in0(REG_2), .in1(REG_2), .out(multiplexer_7_out), .sel(INSTRUCTION[3:2]));  // open: in2, in3
  Multiplexer #(.select(2), .width(8)) multiplexer_8 (
    .in0(8'h1), .in1(random_1_out), .out(multiplexer_8_out), .sel(INSTRUCTION[3:2]));  // open: in2, in3
  Multiplexer #(.select(2), .width(8)) multiplexer_9 (
    .in0(IMMEDIATE), .in1(adder_5_out), .out(multiplexer_9_out), .sel(INSTRUCTION[3:2]));  // open: in2, in3
  Multiplexer #(.select(4), .width(8)) multiplexer_10 (
    .in0(REG_2), .in1(adder_6_out), .in2(subtractor_2_out), .in3(and_3_out), .in4(or_1_out), .in5(xor_1_out),
    .in6(shifter_1_out), .in7(multiplexer_5_out), .in8(REG_2), .in9(REG_1), .in10(REG_1), .in11(REG_1),
    .in12(multiplexer_6_out), .in13(multiplexer_7_out), .in14(multiplexer_8_out), .in15(multiplexer_9_out),
    .out(REG_IN), .sel(INSTRUCTION[7:4]));

  // Other names for the same wires on the sheet: CARRY = in_2; R2_SEL[1:0] = INSTRUCTION[1:0];
  //   REG_C[7:0] = REG_ADDRESS[7:0]; REG_D[7:0] = REG_ADDRESS[15:8]; RESET = in_1; R1_SEL[1:0] = INSTRUCTION[3:2];
  //   SUB_OP[5:0] = INSTRUCTION[7:2]; OPCODE[3:0] = INSTRUCTION[7:4]

  // Notes on the sheet:
  //   TODO read mem
  //   TODO read io
  //   Simple jumps
  //   TODO pop
  //   JE
  //   JG
  //   JL
endmodule
